# Fritzing sketch Karina night light layout (saved by Fritzing 0.8.3b)
breadboards: 1

parts:
  Part1 = Arduino Uno (Rev3)
  R1 = Photocell (LDR) [package=THT]
  R2 = Resistor [tolerance=±5% resistance=470 package=THT]

nets:
  N1: Part1.A0, R1.pin_1, R2.Pin_0
  N2: Part1.GND, R2.Pin_1
  N3: Part1.5V, R1.pin_0

notes:
  Red/Blue/Green Wires go here
